# Fritzing sketch heizung_sketch (saved by Fritzing 0.9.3b)
perfboards: 1

parts:
  U1 = ESP-12F (ESP8266 WiFi Module) [part_number=ESP8266]
  Bauteil1 = Adafruit Micro USB Breakout [part_number="Adafruit #1833"]
  U2 = V_REG_LD1117VXX [part_number=AMS1117 package=78xxl]
  R1 = Resistor [tolerance=±5% resistance=4.7k package=THT]
  R3 = Resistor [tolerance=±5% resistance=4.7k package=THT]
  R4 = Resistor [tolerance=±5% resistance=4.7k package=THT]
  R5 = Resistor [tolerance=±5% resistance=4.7k package=THT]
  J1 = male pin header, 8 pins [form="♂ (male)"]
  J2 = male pin header, 8 pins [form="♂ (male)"]
  U3 = ESP-12F (ESP8266 WiFi Module) [part_number=ESP8266]
  R6 = Resistor [tolerance=±5% resistance=100k package=THT]
  R7 = Resistor [tolerance=±5% resistance=56k package=THT]
  R8 = Photocell (LDR) [package=THT]
  DS1 = DS18B20 1-Wire Temperature Sensor [part_number=DS18B20]
  R9 = Resistor [tolerance=±20% resistance=4.7k package=THT]

nets:
  N1: U1.RXD0, J1.pin2
  N2: U1.VCC, R1.Pin_1, R4.Pin_1, J2.pin8
  N3: U1.GPIO0, R4.Pin_0, J1.pin5
  N4: U1.GPIO2, J1.pin6
  N5: U1.EN, R3.Pin_0, J2.pin3
  N6: U1.GND, R5.Pin_1, J1.pin8
  N7: U1.TXD0, J1.pin1
  N8: U1.GPIO15, R5.Pin_0, J1.pin7
  N9: U1.GPIO4, J1.pin4
  N10: U1.GPIO5, J1.pin3
  N11: U1.ADC0, J2.pin2
  N12: U1.GPIO16, J2.pin4
  N13: U1.GPIO14, J2.pin5
  N14: U1.GPIO12, J2.pin6
  N15: U1.GPIO13, J2.pin7
  N16: U1.RST, R1.Pin_0, J2.pin1
  GND: Bauteil1.GND, U2.GND, U3.GND, R7.Pin_1, R8.pin_1, DS1.GND
  N17: Bauteil1.VBUS, U2.IN
  VCC: U2.OUT, U3.VCC, R6.Pin_0, DS1.VDD, R9.Pin_1
  N18: U3.ADC0, R6.Pin_1, R7.Pin_0, R8.pin_0
  N19: U3.GPIO14, DS1.DQ, R9.Pin_0

custom parts:
  ESP-12F (ESP8266 WiFi Module): WiFi Module based on the ESP8266 with onboard PCB antenna and UART communications
  Adafruit Micro USB Breakout: Simple but effective - this breakout board has a USB Micro-B connector, with all 5 pins broken out. Great for pairing with a microcontroller with USB support, or adding USB 5V power to a project. We use a micro-AB connector with through-hole shielding pads for an excellent strong connection - it won't rip off by accident! Comes with one fully assembled and tested micro B breakout PCB and a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
